# Fritzing sketch EspaceGam_chrono (saved by Fritzing 0.9.4)
breadboards: 1

parts:
  8x8_LED_Modul_mit_MAX4 = 8x8 LED Modul mit MAX7219 [package=THT]
  Composant1 = Arduino Uno (Rev3)
  SP1 = SPEAKER [package=pcb_mount_speaker]  # not connected
  SP2 = SPEAKER [package=pcb_mount_speaker]  # not connected
  8x8_LED_Modul_mit_MAX5 = 8x8 LED Modul mit MAX7219 [package=THT]  # not connected
  8x8_LED_Modul_mit_MAX6 = 8x8 LED Modul mit MAX7219 [package=THT]  # not connected
  8x8_LED_Modul_mit_MAX7 = 8x8 LED Modul mit MAX7219 [package=THT]  # not connected
  BT1 = Bluetooth HC-06d [package=THT]
  S1 = Round Pushbutton
  R1 = Resistor [tolerance=±5% resistance=1k package="1206 [SMD]"]

nets:
  5V: 8x8_LED_Modul_mit_MAX4.VCC_Eingang, Composant1.5V, BT1.VCC, S1.leg1
  GND: 8x8_LED_Modul_mit_MAX4.GND_Eingang, Composant1.GND, BT1.GND, R1.Pin_1
  N1: 8x8_LED_Modul_mit_MAX4.DIN_Eingang, Composant1.D13/SCK
  N2: 8x8_LED_Modul_mit_MAX4.CS_Eingang, Composant1.D12/MISO
  N3: 8x8_LED_Modul_mit_MAX4.CLK_Eingang, Composant1.D11_PWM/MOSI
  N4: Composant1.D9_PWM, BT1.TXD
  N5: Composant1.D10_PWM/SS, BT1.RXD
  N6: Composant1.D7, S1.leg0, R1.Pin_0

custom parts:
  Bluetooth HC-06d: Bluetooth HC-06 - face down, pins down 16.5mm x 37.5mm PCB
